# Fritzing sketch alarm-clock (saved by Fritzing 0.9.3b)

parts:
  DFRobot_DFPlayer_Mini1 = DFRobot DFPlayer Mini [part_number=DFR0299]
  WeMos_D1_Mini_OLED_Shield1 = WeMos D1 Mini OLED Shield
  WeMos_D1_Mini1 = WeMos D1 Mini
  SP1 = SPEAKER [package=pcb_mount_speaker]
  Busy_LED = smd LED [color="White (4500K)" package="1206 [SMD]"]
  Red_Play/Pause = Round Pushbutton
  Green_Next/Vol+ = Round Pushbutton
  Blue_Prev/Vol- = Round Pushbutton

nets:
  VCC: DFRobot_DFPlayer_Mini1.VCC, WeMos_D1_Mini1.5V
  N1: DFRobot_DFPlayer_Mini1.RX, WeMos_D1_Mini1.D5
  N2: DFRobot_DFPlayer_Mini1.TX, WeMos_D1_Mini1.D6
  N3: DFRobot_DFPlayer_Mini1.SPK_1, SP1.-
  N4: DFRobot_DFPlayer_Mini1.GND-1, DFRobot_DFPlayer_Mini1.GND-2, WeMos_D1_Mini_OLED_Shield1.G, WeMos_D1_Mini1.G, Red_Play/Pause.leg1
  N5: DFRobot_DFPlayer_Mini1.SPK_2, SP1.+
  N6: DFRobot_DFPlayer_Mini1.IO_1, Blue_Prev/Vol-.leg0
  N7: DFRobot_DFPlayer_Mini1.IO_2, Green_Next/Vol+.leg0
  N8: DFRobot_DFPlayer_Mini1.BUSY, Busy_LED.cathode, Green_Next/Vol+.leg1, Blue_Prev/Vol-.leg1
  3V3: WeMos_D1_Mini_OLED_Shield1.3V3, WeMos_D1_Mini1.3V3, Busy_LED.anode
  N9: WeMos_D1_Mini_OLED_Shield1.D1, WeMos_D1_Mini1.D1
  N10: WeMos_D1_Mini_OLED_Shield1.D2, WeMos_D1_Mini1.D2
  N11: WeMos_D1_Mini1.D7, Red_Play/Pause.leg0
